// Logisim project ai.circ as structural Verilog: 2 circuits, main circuit AI
module AI (
  input  reset,
  input  [7:0] x,
  input  [7:0] y,
  output [1:0] dir_bat,
  output [4:0] batY
);

  wire _0xf1_out, _0xf2_out, _0xf3_out, and_2_out, cdm_8_mark5_1_p1, cdm_8_mark5_1_p2, cdm_8_mark5_1_p4,
       cdm_8_mark5_1_p5, cdm_8_mark5_1_p6, cdm_8_mark5_1_p7, cdm_8_mark5_1_p8, cdm_8_mark5_1_p9,
       cdm_8_mark5_1_p10, clock, code, data, decoder_1_out1, decoder_1_out2, decoder_1_out3, I_Osel,
       not_1_out, not_2_out, RAM, rd_wr;
  wire [3:0] I_Oadr;
  wire [7:0] cdm_8_mark5_1_p13, cdm_8_mark5_1_p14, I_Odata, register_1_q;
  wire [7:4] cdm_8_mark5_1_p12;

  // Probe on cdm_8_mark5_1_p2
  // Probe on cdm_8_mark5_1_p1
  // Probe on cdm_8_mark5_1_p4
  and and_1 (I_Osel, and_2_out, clock, data);
  Decoder #(.select(4), .enable("false")) decoder_1 (
    .out1(decoder_1_out1), .out2(decoder_1_out2), .out3(decoder_1_out3), .sel(I_Oadr));  // open: out0, out4, out5, out6, out7, out8, out9, out10, out11, out12, out13, out14, out15
  // Probe on cdm_8_mark5_1_p5
  Clock clock_1 (.out(clock));
  // Probe on cdm_8_mark5_1_p7
  // Probe on cdm_8_mark5_1_p6
  // Probe on cdm_8_mark5_1_p8
  // CdM_8_mark5 cdm_8_mark5_1: pin names not known; wires that end beside it: cdm_8_mark5_1_p1, cdm_8_mark5_1_p2, clock, cdm_8_mark5_1_p4, cdm_8_mark5_1_p5, cdm_8_mark5_1_p6, cdm_8_mark5_1_p7, cdm_8_mark5_1_p8, cdm_8_mark5_1_p9, cdm_8_mark5_1_p10, rd_wr, {cdm_8_mark5_1_p12, I_Oadr}, cdm_8_mark5_1_p13, cdm_8_mark5_1_p14
  and and_2 (and_2_out, cdm_8_mark5_1_p12[4], cdm_8_mark5_1_p12[5], cdm_8_mark5_1_p12[6], cdm_8_mark5_1_p12[7]);
  Decoder #(.disabled(0)) decoder_2 (.out0(code), .out1(data), .sel(cdm_8_mark5_1_p9), .en(cdm_8_mark5_1_p10));
  assign I_Odata = not_1_out ? cdm_8_mark5_1_p13 : 8'bz;  // Controlled_Buffer controlled_buffer_1
  not not_1 (not_1_out, rd_wr);
  assign cdm_8_mark5_1_p14 = rd_wr ? I_Odata : 8'bz;  // Controlled_Buffer controlled_buffer_2
  and _0xf1 (_0xf1_out, decoder_1_out1, ~rd_wr, I_Osel);  // AND_Gate
  and _0xf2 (_0xf2_out, decoder_1_out2, rd_wr, I_Osel);
  and _0xf3 (_0xf3_out, decoder_1_out3, rd_wr, I_Osel);
  and and_3 (RAM, data, not_2_out);
  not not_2 (not_2_out, I_Osel);
  Register register_1 (.D(I_Odata), .Q(register_1_q), .clk(_0xf1_out));  // open: en, clr
  assign I_Odata = _0xf2_out ? x : 8'bz;  // Controlled_Buffer controlled_buffer_3
  assign I_Odata = _0xf3_out ? y : 8'bz;  // Controlled_Buffer controlled_buffer_4
  // Probe on {cdm_8_mark5_1_p12, I_Oadr}
  steps steps_1 (.batY_in(register_1_q[4:0]), .tact(clock), .batY_out(batY), .reset(reset), .dir_bat(dir_bat));
  ROM rom_1 (.addr({cdm_8_mark5_1_p12, I_Oadr}), .data(I_Odata), .sel(code));
  RAM #(.bus("separate")) ram_1 (
    .addr({cdm_8_mark5_1_p12, I_Oadr}), .din(I_Odata), .data(I_Odata), .sel(RAM), .clk(clock), .ld(rd_wr),
    .clr(reset));  // open: str
  // Probe on I_Odata
  // also tied to GND on the sheet: {register_1_q[5], register_1_q[6], register_1_q[7]}

  // Notes on the sheet:
  //   contents of rom_1 (hex, n*v repeats v):
  //   cd f0 d2 f3 d1 f2 b5 ba 7 d0 1f 41 5*9b f e0 3f b d0 1f 42 5*9b f e0 31 d0 1d 31 99 d3 1f 16 7e ea
  //   2f 3b d2 1f 3b e ee 3d d0 1d 31 99 79 ea 3b 36 ee 3d 39 6 ee 41 d2 e d0 f1 a2 ee 2 d4 3c 2d
endmodule

module steps (
  input  reset,
  input  tact,
  input  [4:0] batY_in,
  output [4:0] batY_out,
  output [1:0] dir_bat
);

  wire clock_1_out, d_ff_1_q, d_ff_2_q, not_1_out, not_2_out;
  wire [2:0] comparator_1_gt, comparator_2_gt;
  wire [4:0] adder_1_out, multiplexer_1_out, multiplexer_2_out, subtractor_1_out;

  Comparator #(.width(5)) comparator_1 (
    .a(batY_in), .b({5{1'b0}}), .gt(comparator_1_gt[0]), .eq(comparator_1_gt[1]), .lt(comparator_1_gt[2]));
  // Probe on subtractor_1_out
  Subtractor #(.width(5)) subtractor_1 (.a(batY_in), .b(5'b00001), .out(subtractor_1_out));  // open: bin, bout
  Multiplexer #(.select(3), .width(5), .enable("false")) multiplexer_1 (
    .in1(subtractor_1_out), .in2({5{1'b0}}), .in4({5{1'b0}}), .out(multiplexer_1_out), .sel(comparator_1_gt));  // open: in0, in3, in5, in6, in7
  Comparator #(.width(5)) comparator_2 (
    .a(multiplexer_1_out), .b(batY_out), .gt(comparator_2_gt[0]), .eq(comparator_2_gt[1]),
    .lt(comparator_2_gt[2]));
  Multiplexer #(.select(3), .width(5), .enable("false")) multiplexer_2 (
    .in1(5'b00001), .in2({5{1'b0}}), .in4({5{1'b1}}), .out(multiplexer_2_out), .sel(comparator_2_gt));  // open: in0, in3, in5, in6, in7
  Clock clock_1 (.out(clock_1_out));
  Multiplexer #(.select(3), .width(2), .enable("false")) multiplexer_3 (
    .in1(2'b01), .in2(2'b00), .in4(2'b10), .out(dir_bat), .sel(comparator_2_gt));  // open: in0, in3, in5, in6, in7
  Adder #(.width(5)) adder_1 (.a(batY_out), .b(multiplexer_2_out), .out(adder_1_out));  // open: cin, cout
  D_Flip_Flop d_ff_1 (.clk(clock_1_out), .D(not_1_out), .Q(d_ff_1_q));  // open: Qn, preset, en, reset
  Register #(.width(5)) register_1 (.D(adder_1_out), .Q(batY_out), .clk(d_ff_1_q), .clr(reset));  // open: en
  not not_1 (not_1_out, d_ff_1_q);
  D_Flip_Flop d_ff_2 (.clk(not_1_out), .D(not_2_out), .Q(d_ff_2_q));  // open: Qn, preset, en, reset
  not not_2 (not_2_out, d_ff_2_q);
endmodule
