// Logisim project klava.circ as structural Verilog: 4 circuits, main circuit MAIN
module main (
  input  [4:0] ROW,
  input  [4:0] ballX,
  input  [4:0] ballY,
  input  [4:0] leftbatY,
  input  [4:0] rightbatY,
  output [4:0] NEXT_ROW,
  output [4:0] out_7,
  output [4:0] out_8,
  output [4:0] out_9,
  output [4:0] out_10,
  output [31:0] out_11
);

  wire comparator_1_eq, comparator_2_eq, comparator_3_eq, xor_1_out;
  wire [4:0] mux;
  wire [31:0] decoder_1_out0, decoder_2_out30;

  Adder #(.width(5)) adder_1 (.a(5'b00001), .b(ROW), .out(NEXT_ROW));  // open: cin, cout
  Comparator #(.width(5)) comparator_1 (.a(ROW), .b(ballX), .eq(comparator_1_eq));  // open: gt, lt
  Comparator #(.width(5)) comparator_2 (.a(ROW), .b(5'b00010), .eq(comparator_2_eq));  // open: gt, lt
  Comparator #(.width(5)) comparator_3 (.a(ROW), .b(5'b11101), .eq(comparator_3_eq));  // open: gt, lt
  Multiplexer #(.width(5)) multiplexer_1 (
    .in0(leftbatY), .in1(rightbatY), .out(mux), .sel(comparator_3_eq), .en(xor_1_out));
  xor xor_1 (xor_1_out, comparator_2_eq, comparator_3_eq);
  Decoder #(.select(5)) decoder_1 (
    .out0(decoder_1_out0[0]), .out1(decoder_1_out0[1]), .out2(decoder_1_out0[2]), .out3(decoder_1_out0[3]),
    .out4(decoder_1_out0[4]), .out5(decoder_1_out0[5]), .out6(decoder_1_out0[6]), .out7(decoder_1_out0[7]),
    .out8(decoder_1_out0[8]), .out9(decoder_1_out0[9]), .out10(decoder_1_out0[10]),
    .out11(decoder_1_out0[11]), .out12(decoder_1_out0[12]), .out13(decoder_1_out0[13]),
    .out14(decoder_1_out0[14]), .out15(decoder_1_out0[15]), .out16(decoder_1_out0[16]),
    .out17(decoder_1_out0[17]), .out18(decoder_1_out0[18]), .out19(decoder_1_out0[19]),
    .out20(decoder_1_out0[20]), .out21(decoder_1_out0[21]), .out22(decoder_1_out0[22]),
    .out23(decoder_1_out0[23]), .out24(decoder_1_out0[24]), .out25(decoder_1_out0[25]),
    .out26(decoder_1_out0[26]), .out27(decoder_1_out0[27]), .out28(decoder_1_out0[28]),
    .out29(decoder_1_out0[29]), .out30(decoder_1_out0[30]), .out31(decoder_1_out0[31]), .sel(ballY),
    .en(comparator_1_eq));
  Decoder #(.select(5)) decoder_2 (
    .out0(decoder_2_out30[0]), .out1(decoder_2_out30[1]), .out2(decoder_2_out30[2]),
    .out3(decoder_2_out30[3]), .out4(decoder_2_out30[4]), .out5(decoder_2_out30[5]),
    .out6(decoder_2_out30[6]), .out7(decoder_2_out30[7]), .out8(decoder_2_out30[8]),
    .out9(decoder_2_out30[9]), .out10(decoder_2_out30[10]), .out11(decoder_2_out30[11]),
    .out12(decoder_2_out30[12]), .out13(decoder_2_out30[13]), .out14(decoder_2_out30[14]),
    .out15(decoder_2_out30[15]), .out16(decoder_2_out30[16]), .out17(decoder_2_out30[17]),
    .out18(decoder_2_out30[18]), .out19(decoder_2_out30[19]), .out20(decoder_2_out30[20]),
    .out21(decoder_2_out30[21]), .out22(decoder_2_out30[22]), .out23(decoder_2_out30[23]),
    .out24(decoder_2_out30[24]), .out25(decoder_2_out30[25]), .out26(decoder_2_out30[26]),
    .out27(decoder_2_out30[27]), .out28(decoder_2_out30[28]), .out29(decoder_2_out30[29]),
    .out30(decoder_2_out30[30]), .out31(decoder_2_out30[31]), .sel(mux), .en(xor_1_out));
  Pull_Resistor pull_resistor_1 (.node(decoder_1_out0));
  Pull_Resistor pull_resistor_2 (.node(decoder_2_out30));
  assign out_11 = decoder_1_out0 | decoder_2_out30 | {decoder_2_out30[30:0], 1'b0} | {decoder_2_out30[29:0], 2'b00};  // OR_Gate or_1, 32 bits wide

  assign out_7 = ballX;
  assign out_8 = ballY;
  assign out_9 = leftbatY;
  assign out_10 = rightbatY;
endmodule

module _8rows (
  input  [4:0] in_1,
  input  [4:0] in_2,
  input  [4:0] in_3,
  input  [4:0] in_4,
  input  [4:0] in_5,
  output [31:0] out_6,
  output [31:0] out_7,
  output [31:0] out_8,
  output [31:0] out_9,
  output [31:0] out_10,
  output [31:0] out_11,
  output [31:0] out_12,
  output [31:0] out_13,
  output [4:0] out_14,
  output [4:0] out_15,
  output [4:0] out_16,
  output [4:0] out_17,
  output [4:0] out_18
);

  wire [4:0] main_1_next_row, main_1_out_7, main_1_out_8, main_1_out_9, main_1_out_10, main_2_next_row,
       main_2_out_7, main_2_out_8, main_2_out_9, main_2_out_10, main_3_next_row, main_3_out_7, main_3_out_8,
       main_3_out_9, main_3_out_10, main_4_next_row, main_4_out_7, main_4_out_8, main_4_out_9, main_4_out_10,
       main_5_next_row, main_5_out_7, main_5_out_8, main_5_out_9, main_5_out_10, main_6_next_row,
       main_6_out_7, main_6_out_8, main_6_out_9, main_6_out_10, main_7_next_row, main_7_out_7, main_7_out_8,
       main_7_out_9, main_7_out_10;

  main main_1 (
    .ROW(in_1), .ballX(in_2), .out_7(main_1_out_7), .ballY(in_3), .out_8(main_1_out_8), .leftbatY(in_4),
    .out_9(main_1_out_9), .rightbatY(in_5), .out_10(main_1_out_10), .NEXT_ROW(main_1_next_row), .out_11(out_6));
  main main_2 (
    .ROW(main_1_next_row), .ballX(main_1_out_7), .out_7(main_2_out_7), .ballY(main_1_out_8),
    .out_8(main_2_out_8), .leftbatY(main_1_out_9), .out_9(main_2_out_9), .rightbatY(main_1_out_10),
    .out_10(main_2_out_10), .NEXT_ROW(main_2_next_row), .out_11(out_7));
  main main_3 (
    .ROW(main_2_next_row), .ballX(main_2_out_7), .out_7(main_3_out_7), .ballY(main_2_out_8),
    .out_8(main_3_out_8), .leftbatY(main_2_out_9), .out_9(main_3_out_9), .rightbatY(main_2_out_10),
    .out_10(main_3_out_10), .NEXT_ROW(main_3_next_row), .out_11(out_8));
  main main_4 (
    .ROW(main_3_next_row), .ballX(main_3_out_7), .out_7(main_4_out_7), .ballY(main_3_out_8),
    .out_8(main_4_out_8), .leftbatY(main_3_out_9), .out_9(main_4_out_9), .rightbatY(main_3_out_10),
    .out_10(main_4_out_10), .NEXT_ROW(main_4_next_row), .out_11(out_9));
  main main_5 (
    .ROW(main_4_next_row), .ballX(main_4_out_7), .out_7(main_5_out_7), .ballY(main_4_out_8),
    .out_8(main_5_out_8), .leftbatY(main_4_out_9), .out_9(main_5_out_9), .rightbatY(main_4_out_10),
    .out_10(main_5_out_10), .NEXT_ROW(main_5_next_row), .out_11(out_10));
  main main_6 (
    .ROW(main_5_next_row), .ballX(main_5_out_7), .out_7(main_6_out_7), .ballY(main_5_out_8),
    .out_8(main_6_out_8), .leftbatY(main_5_out_9), .out_9(main_6_out_9), .rightbatY(main_5_out_10),
    .out_10(main_6_out_10), .NEXT_ROW(main_6_next_row), .out_11(out_11));
  main main_7 (
    .ROW(main_6_next_row), .ballX(main_6_out_7), .out_7(main_7_out_7), .ballY(main_6_out_8),
    .out_8(main_7_out_8), .leftbatY(main_6_out_9), .out_9(main_7_out_9), .rightbatY(main_6_out_10),
    .out_10(main_7_out_10), .NEXT_ROW(main_7_next_row), .out_11(out_12));
  main main_8 (
    .ROW(main_7_next_row), .ballX(main_7_out_7), .out_7(out_15), .ballY(main_7_out_8), .out_8(out_16),
    .leftbatY(main_7_out_9), .out_9(out_17), .rightbatY(main_7_out_10), .out_10(out_18), .NEXT_ROW(out_14),
    .out_11(out_13));
endmodule

module MAIN (
  input  [4:0] in_1,
  input  [4:0] in_2,
  input  [4:0] in_3,
  input  [4:0] in_4,
  input  [4:0] in_5
);

  wire clock_1_out;
  wire [4:0] n8rows_1_out_14, n8rows_1_out_15, n8rows_1_out_16, n8rows_1_out_17, n8rows_1_out_18,
       n8rows_2_out_14, n8rows_2_out_15, n8rows_2_out_16, n8rows_2_out_17, n8rows_2_out_18, n8rows_3_out_14,
       n8rows_3_out_15, n8rows_3_out_16, n8rows_3_out_17, n8rows_3_out_18;
  wire [6:0] keyboard_1_data;
  wire [31:0] n8rows_1_out_6, n8rows_1_out_7, n8rows_1_out_8, n8rows_1_out_9, n8rows_1_out_10,
       n8rows_1_out_11, n8rows_1_out_12, n8rows_1_out_13, n8rows_2_out_6, n8rows_2_out_7, n8rows_2_out_8,
       n8rows_2_out_9, n8rows_2_out_10, n8rows_2_out_11, n8rows_2_out_12, n8rows_2_out_13, n8rows_3_out_6,
       n8rows_3_out_7, n8rows_3_out_8, n8rows_3_out_9, n8rows_3_out_10, n8rows_3_out_11, n8rows_3_out_12,
       n8rows_3_out_13, n8rows_4_out_6, n8rows_4_out_7, n8rows_4_out_8, n8rows_4_out_9, n8rows_4_out_10,
       n8rows_4_out_11, n8rows_4_out_12, n8rows_4_out_13;

  Clock clock_1 (.out(clock_1_out));
  Keyboard keyboard_1 (.clk(clock_1_out), .data(keyboard_1_data));  // open: re, clr, avail
  Hex_Digit_Display hex_digit_display_1 ();  // open: value, dp
  Hex_Digit_Display hex_digit_display_2 ();  // open: value, dp
  _8rows u_8rows_1 (
    .in_1(in_1), .in_2(in_2), .in_3(in_3), .in_4(in_4), .in_5(in_5), .out_6(n8rows_1_out_6),
    .out_7(n8rows_1_out_7), .out_8(n8rows_1_out_8), .out_9(n8rows_1_out_9), .out_10(n8rows_1_out_10),
    .out_11(n8rows_1_out_11), .out_12(n8rows_1_out_12), .out_13(n8rows_1_out_13), .out_14(n8rows_1_out_14),
    .out_15(n8rows_1_out_15), .out_16(n8rows_1_out_16), .out_17(n8rows_1_out_17), .out_18(n8rows_1_out_18));
  DotMatrix #(.matrixcols(32), .matrixrows(32)) dotmatrix_1 (
    .col0(n8rows_1_out_6), .col1(n8rows_1_out_7), .col2(n8rows_1_out_8), .col3(n8rows_1_out_9),
    .col4(n8rows_1_out_10), .col5(n8rows_1_out_11), .col6(n8rows_1_out_12), .col7(n8rows_1_out_13),
    .col8(n8rows_2_out_6), .col9(n8rows_2_out_7), .col10(n8rows_2_out_8), .col11(n8rows_2_out_9),
    .col12(n8rows_2_out_10), .col13(n8rows_2_out_11), .col14(n8rows_2_out_12), .col15(n8rows_2_out_13),
    .col16(n8rows_3_out_6), .col17(n8rows_3_out_7), .col18(n8rows_3_out_8), .col19(n8rows_3_out_9),
    .col20(n8rows_3_out_10), .col21(n8rows_3_out_11), .col22(n8rows_3_out_12), .col23(n8rows_3_out_13),
    .col24(n8rows_4_out_6), .col25(n8rows_4_out_7), .col26(n8rows_4_out_8), .col27(n8rows_4_out_9),
    .col28(n8rows_4_out_10), .col29(n8rows_4_out_11), .col30(n8rows_4_out_12), .col31(n8rows_4_out_13));
  _8rows u_8rows_2 (
    .in_1(n8rows_1_out_14), .in_2(n8rows_1_out_15), .in_3(n8rows_1_out_16), .in_4(n8rows_1_out_17),
    .in_5(n8rows_1_out_18), .out_6(n8rows_2_out_6), .out_7(n8rows_2_out_7), .out_8(n8rows_2_out_8),
    .out_9(n8rows_2_out_9), .out_10(n8rows_2_out_10), .out_11(n8rows_2_out_11), .out_12(n8rows_2_out_12),
    .out_13(n8rows_2_out_13), .out_14(n8rows_2_out_14), .out_15(n8rows_2_out_15), .out_16(n8rows_2_out_16),
    .out_17(n8rows_2_out_17), .out_18(n8rows_2_out_18));
  _8rows u_8rows_3 (
    .in_1(n8rows_2_out_14), .in_2(n8rows_2_out_15), .in_3(n8rows_2_out_16), .in_4(n8rows_2_out_17),
    .in_5(n8rows_2_out_18), .out_6(n8rows_3_out_6), .out_7(n8rows_3_out_7), .out_8(n8rows_3_out_8),
    .out_9(n8rows_3_out_9), .out_10(n8rows_3_out_10), .out_11(n8rows_3_out_11), .out_12(n8rows_3_out_12),
    .out_13(n8rows_3_out_13), .out_14(n8rows_3_out_14), .out_15(n8rows_3_out_15), .out_16(n8rows_3_out_16),
    .out_17(n8rows_3_out_17), .out_18(n8rows_3_out_18));
  _8rows u_8rows_4 (
    .in_1(n8rows_3_out_14), .in_2(n8rows_3_out_15), .in_3(n8rows_3_out_16), .in_4(n8rows_3_out_17),
    .in_5(n8rows_3_out_18), .out_6(n8rows_4_out_6), .out_7(n8rows_4_out_7), .out_8(n8rows_4_out_8),
    .out_9(n8rows_4_out_9), .out_10(n8rows_4_out_10), .out_11(n8rows_4_out_11), .out_12(n8rows_4_out_12),
    .out_13(n8rows_4_out_13));  // open: out_14, out_15, out_16, out_17, out_18
  Hex_Digit_Display hex_digit_display_3 ();  // open: value, dp
  Hex_Digit_Display hex_digit_display_4 ();  // open: value, dp
endmodule

module keyboard (
  input  [6:0] in_1,
  output [1:0] out_2
);

  wire comparator_1_eq, comparator_2_eq, comparator_3_eq, comparator_4_eq;

  Comparator #(.width(7)) comparator_1 (.a(in_1), .b(7'b1110111), .eq(comparator_1_eq));  // open: gt, lt
  Comparator #(.width(7)) comparator_2 (.a(in_1), .b(7'b1000110), .eq(comparator_2_eq));  // open: gt, lt
  Comparator #(.width(7)) comparator_3 (.a(in_1), .b(7'b1110011), .eq(comparator_3_eq));  // open: gt, lt
  Comparator #(.width(7)) comparator_4 (.a(in_1), .b(7'b1001011), .eq(comparator_4_eq));  // open: gt, lt
  or or_1 (out_2[0], comparator_1_eq, comparator_2_eq);
  or or_2 (out_2[1], comparator_3_eq, comparator_4_eq);

  // Notes on the sheet:
  //   ascii w
  //   ascii ц
  //   ascii s
  //   ascii ы
  //   UP
  //   DOWN
endmodule
