// Logisim project tennis.circ as structural Verilog: 7 circuits, main circuit main
module main (
  input  combo,
  input  nonstop,
  input  AI,
  input  AI_hard_level
);

  wire clk, control_1_double_speed, res, screen_1_move;
  wire [4:0] control_1_lb, control_1_rb, control_1_x, control_1_y;
  wire [6:0] keyboard_1_data;
  wire [7:0] combo_t, Lscore, Rscore;
  wire [31:0] screen_1_color, screen_1_out_9, screen_1_out_10, screen_1_out_11, screen_1_out_12,
       screen_1_out_13, screen_1_out_14, screen_1_out_15, screen_1_out_16, screen_1_out_17, screen_1_out_18,
       screen_1_out_19, screen_1_out_20, screen_1_out_21, screen_1_out_22, screen_1_out_23, screen_1_out_24,
       screen_1_out_25, screen_1_out_26, screen_1_out_27, screen_1_out_28, screen_1_out_29, screen_1_out_30,
       screen_1_out_31, screen_1_out_32, screen_1_out_33, screen_1_out_34, screen_1_out_35, screen_1_out_36,
       screen_1_out_37, screen_1_out_38, screen_1_out_39, screen_1_out_41;

  Clock clock_1 (.out(clk));
  Keyboard keyboard_1 (.clk(clk), .data(keyboard_1_data));  // open: re, clr, avail
  Button r (.out(res));
  Hex_Digit_Display hex_digit_display_1 (.value(Lscore[7:4]));  // open: dp
  Hex_Digit_Display hex_digit_display_2 (.value(Lscore[3:0]));  // open: dp
  control control_1 (
    .res(res), .kin(keyboard_1_data), .x(control_1_x), .lb(control_1_lb), .clk(clk), .y(control_1_y),
    .rb(control_1_rb), .enemyscore(Rscore), .myscore(Lscore), .AI(AI), .nonstop(nonstop), .combo(combo),
    .double_speed(control_1_double_speed), .combo_score(combo_t), .move(screen_1_move), .lvl(AI_hard_level));
  DotMatrix #(.matrixcols(1), .matrixrows(32)) dotmatrix_1 (.col0(screen_1_color));
  screen screen_1 (
    .ballx(control_1_x), .bally(control_1_y), .left_bat(control_1_lb), .right_bat(control_1_rb),
    .out_38(screen_1_out_38), .out_36(screen_1_out_36), .out_34(screen_1_out_34), .out_32(screen_1_out_32),
    .out_30(screen_1_out_30), .out_28(screen_1_out_28), .out_26(screen_1_out_26), .out_9(screen_1_out_9),
    .out_10(screen_1_out_10), .out_11(screen_1_out_11), .out_12(screen_1_out_12), .out_13(screen_1_out_13),
    .out_14(screen_1_out_14), .out_15(screen_1_out_15), .out_16(screen_1_out_16), .out_17(screen_1_out_17),
    .out_18(screen_1_out_18), .out_19(screen_1_out_19), .out_20(screen_1_out_20), .out_21(screen_1_out_21),
    .out_22(screen_1_out_22), .out_23(screen_1_out_23), .out_24(screen_1_out_24), .out_25(screen_1_out_25),
    .out_27(screen_1_out_27), .out_29(screen_1_out_29), .out_31(screen_1_out_31), .out_33(screen_1_out_33),
    .out_35(screen_1_out_35), .out_37(screen_1_out_37), .out_39(screen_1_out_39), .out_41(screen_1_out_41),
    .res(res), .color(screen_1_color), .combo(control_1_double_speed), .lscore(Lscore), .rscore(Rscore),
    .move(screen_1_move));
  DotMatrix #(.matrixcols(32), .matrixrows(32)) dotmatrix_2 (
    .col0(screen_1_out_38), .col1(screen_1_out_36), .col2(screen_1_out_34), .col3(screen_1_out_32),
    .col4(screen_1_out_30), .col5(screen_1_out_28), .col6(screen_1_out_26), .col7(screen_1_out_9),
    .col8(screen_1_out_10), .col9(screen_1_out_11), .col10(screen_1_out_12), .col11(screen_1_out_13),
    .col12(screen_1_out_14), .col13(screen_1_out_15), .col14(screen_1_out_16), .col15(screen_1_out_17),
    .col16(screen_1_out_18), .col17(screen_1_out_19), .col18(screen_1_out_20), .col19(screen_1_out_21),
    .col20(screen_1_out_22), .col21(screen_1_out_23), .col22(screen_1_out_24), .col23(screen_1_out_25),
    .col24(screen_1_out_27), .col25(screen_1_out_29), .col26(screen_1_out_31), .col27(screen_1_out_33),
    .col28(screen_1_out_35), .col29(screen_1_out_37), .col30(screen_1_out_39), .col31(screen_1_out_41));
  Hex_Digit_Display hex_digit_display_3 (.value(Rscore[7:4]));  // open: dp
  Hex_Digit_Display hex_digit_display_4 (.value(Rscore[3:0]));  // open: dp
  DotMatrix #(.matrixcols(1), .matrixrows(32)) dotmatrix_3 (.col0(screen_1_color));
  Hex_Digit_Display hex_digit_display_5 (.value(combo_t[7:4]));  // open: dp
  Hex_Digit_Display hex_digit_display_6 (.value(combo_t[3:0]));  // open: dp

  // Other names for the same wires on the sheet: ailvl = AI_hard_level; cmb = combo; nn = nonstop

  // Notes on the sheet:
  //   Combo
  //   Settings
endmodule

module control (
  input  lvl,
  input  res,
  input  AI,
  input  nonstop,
  input  [6:0] kin,
  input  clk,
  input  move,
  input  combo,
  output [4:0] y,
  output [4:0] lb,
  output [4:0] rb,
  output [4:0] x,
  output [7:0] myscore,
  output [7:0] enemyscore,
  output [7:0] combo_score,
  output double_speed
);

  wire _2clk, _4clk, _8clk, _16clk, _32clk, ad, and_1_out, and_2_out, and_3_out, and_4_out, and_6_out,
       and_7_out, and_8_out, and_9_out, and_10_out, cmb, collision, collision_1_collision,
       collision_2_collision, comparator_1_eq, comparator_2_eq, comparator_3_lt, comparator_4_eq,
       comparator_5_eq, comparator_6_eq, controlled_buffer_2_out, controlled_inverter_1_out, d_ff_1_q,
       d_ff_2_q, d_ff_3_q, d_ff_4_q, d_ff_5_q, da, goal1, goal2, multiplexer_2_out, multiplexer_3_out,
       multiplexer_4_out, multiplexer_8_out, multiplexer_10_out, multiplexer_11_out, multiplexer_12_out,
       multiplexer_14_out, multiplexer_15_out, not_1_out, not_2_out, not_3_out, not_5_out, not_8_out,
       or_1_out, or_2_out, or_3_out, or_4_out, or_6_out, or_8_out, or_10_out, or_11_out,
       pull_resistor_2_node, register_1_q, register_2_q, state, vx, vy, xor_1_out;
  wire [1:0] ai_1_dir_bat, keyboard_1_dir, multiplexer_6_out, rstep_1_dir, state_q;
  wire [1:1] multiplexer_5_out;
  wire [2:0] controlled_buffer_1_out, multiplexer_1_out;
  wire [4:0] adder_4_out, adder_5_out, ai_1_baty, controlled_buffer_6_out, controlled_buffer_8_out,
       multiplexer_7_out, multiplexer_9_out, multiplexer_13_out, rstep_1_rbat;
  wire [7:0] adder_1_out, adder_2_out, adder_3_out;

  assign controlled_buffer_1_out = ad ? {1'b1, state_q} : 3'bz;  // Controlled_Buffer controlled_buffer_1
  not not_1 (not_1_out, nonstop);
  assign controlled_buffer_2_out = not_1_out ? or_1_out : 1'bz;  // Controlled_Buffer controlled_buffer_2
  Pull_Resistor pull_resistor_1 (.node(controlled_buffer_2_out));
  or or_1 (or_1_out, goal2, goal1);
  Adder adder_1 (.a(8'h6), .b(myscore), .out(adder_1_out));  // open: cin, cout
  Adder adder_2 (.a(8'h6), .b(enemyscore), .out(adder_2_out));  // open: cin, cout
  Adder adder_3 (.a(8'h6), .b(combo_score), .out(adder_3_out));  // open: cin, cout
  Multiplexer #(.width(3), .enable("false")) multiplexer_1 (
    .in0(controlled_buffer_1_out), .in1(3'b000), .out(multiplexer_1_out), .sel(and_1_out));
  and and_1 (and_1_out, controlled_buffer_2_out, ~ad);  // AND_Gate
  and and_2 (and_2_out, goal1, move);
  and and_3 (and_3_out, goal2, move);
  AI ai_1 (
    .reset(res), .x({2'b00, vx, x}), .y({2'b00, vy, y}), .batY(ai_1_baty), .dir_bat(ai_1_dir_bat),
    .state(state), .level(lvl), .double_speed(double_speed));
  or or_2 (or_2_out, res, ~state);  // OR_Gate
  Register #(.width(3)) u_state (.D(multiplexer_1_out), .Q({state, state_q}), .clk(clk), .clr(res));  // open: en
  Counter counter_1 (
    .load(comparator_1_eq), .D(adder_1_out), .count(and_2_out), .Q(myscore), .clk(multiplexer_2_out),
    .clr(res));  // open: carry
  Multiplexer #(.enable("false")) multiplexer_2 (
    .in0(_16clk), .in1(_8clk), .out(multiplexer_2_out), .sel(double_speed));
  Counter counter_2 (
    .load(comparator_2_eq), .D(adder_2_out), .count(and_3_out), .Q(enemyscore), .clk(multiplexer_3_out),
    .clr(res));  // open: carry
  Multiplexer #(.enable("false")) multiplexer_3 (
    .in0(_16clk), .in1(_8clk), .out(multiplexer_3_out), .sel(double_speed));
  Counter counter_3 (
    .D(adder_3_out), .count(and_4_out), .Q(combo_score), .clk(multiplexer_4_out), .clr(or_3_out));  // open: load, carry
  and and_4 (and_4_out, cmb, move);
  Multiplexer #(.enable("false")) multiplexer_4 (
    .in0(_16clk), .in1(_8clk), .out(multiplexer_4_out), .sel(double_speed));
  or or_3 (or_3_out, goal1, res, goal2);
  rstep rstep_1 (.keyb(kin), .clk(clk), .rs(or_2_out), .rBat(rstep_1_rbat), .dir(rstep_1_dir));
  not not_2 (not_2_out, AI);
  Comparator #(.width(4)) comparator_1 (.a(myscore[3:0]), .b(4'b1010), .eq(comparator_1_eq));  // open: gt, lt
  Comparator #(.width(4)) comparator_2 (.a(enemyscore[3:0]), .b(4'b1010), .eq(comparator_2_eq));  // open: gt, lt
  Comparator comparator_3 (.a(8'h4), .b(combo_score), .lt(comparator_3_lt));  // open: gt, eq
  assign rb = AI ? ai_1_baty : 5'bz;  // Controlled_Buffer controlled_buffer_3
  assign rb = not_2_out ? rstep_1_rbat : 5'bz;  // Controlled_Buffer controlled_buffer_4
  Register #(.width(1)) register_1 (.D(goal2), .en(goal2), .Q(register_1_q), .clk(clk), .clr(goal1));
  and and_5 (double_speed, comparator_3_lt, combo);
  keyboard keyboard_1 (.keyb(kin), .dir(keyboard_1_dir));
  or or_4 (or_4_out, res, ~state);  // OR_Gate
  Multiplexer #(.width(2), .enable("false")) multiplexer_5 (
    .in0(multiplexer_6_out), .in1(keyboard_1_dir), .out({multiplexer_5_out[1], da}), .sel(register_1_q));
  or or_5 (ad, multiplexer_5_out[1], da);
  lstep lstep_1 (.clk(clk), .dir(keyboard_1_dir), .rs(or_4_out), .lBat(lb));
  Multiplexer #(.width(2), .enable("false")) multiplexer_6 (
    .in0(rstep_1_dir), .in1(ai_1_dir_bat), .out(multiplexer_6_out), .sel(AI));
  Comparator #(.width(5)) comparator_4 (.a(y), .b({5{1'b0}}), .eq(comparator_4_eq));  // open: gt, lt
  Comparator #(.width(5)) comparator_5 (.a(y), .b({5{1'b1}}), .eq(comparator_5_eq));  // open: gt, lt
  Comparator #(.width(5)) comparator_6 (.a(x), .b({5{1'b0}}), .eq(comparator_6_eq));  // open: gt, lt
  Comparator #(.width(5)) comparator_7 (.a(x), .b({5{1'b1}}), .eq(goal1));  // open: gt, lt
  collision collision_1 (.bat(lb), .yball(y), .collision(collision_1_collision), .xball(x), .in(5'b00010));
  collision collision_2 (.bat(rb), .yball(y), .collision(collision_2_collision), .xball(x), .in(5'b11101));
  or or_6 (or_6_out, comparator_4_eq, comparator_5_eq);
  Adder #(.width(5)) adder_4 (.a(x), .b(multiplexer_7_out), .out(adder_4_out));  // open: cin, cout
  Multiplexer #(.width(5), .enable("false")) multiplexer_7 (
    .in0({5{1'b1}}), .in1(5'b00001), .out(multiplexer_7_out), .sel(xor_1_out));
  xor xor_1 (xor_1_out, vx, collision);
  not not_3 (not_3_out, state);
  Pull_Resistor #(.pull(1)) pull_resistor_2 (.node(pull_resistor_2_node));
  assign pull_resistor_2_node = state ? or_6_out : 1'bz;  // Controlled_Buffer controlled_buffer_5
  or or_7 (collision, comparator_6_eq, collision_1_collision, goal1, collision_2_collision);
  D_Flip_Flop d_ff_1 (.clk(clk), .D(_2clk), .Q(d_ff_1_q));  // open: Qn, preset, en, reset
  not not_4 (_2clk, d_ff_1_q);
  assign controlled_buffer_6_out = and_6_out ? 5'b00011 : 5'bz;  // Controlled_Buffer controlled_buffer_6
  and and_6 (and_6_out, goal2, not_5_out);
  not not_5 (not_5_out, state);
  Multiplexer #(.enable("false")) multiplexer_8 (
    .in0(comparator_4_eq), .in1(da), .out(multiplexer_8_out), .sel(not_3_out));
  or or_8 (or_8_out, comparator_6_eq, collision_1_collision);
  and and_7 (and_7_out, collision_1_collision, ~vx);  // AND_Gate
  and and_8 (and_8_out, vx, collision_2_collision);
  not not_6 (_4clk, d_ff_2_q);
  D_Flip_Flop d_ff_2 (.clk(_2clk), .D(_4clk), .Q(d_ff_2_q));  // open: Qn, preset, en, reset
  Multiplexer #(.width(5), .enable("false")) multiplexer_9 (
    .in0({5{1'b1}}), .in1(5'b00001), .out(multiplexer_9_out), .sel(vy));
  and and_9 (and_9_out, not_5_out, goal1);
  assign controlled_buffer_6_out = state ? adder_4_out : 5'bz;  // Controlled_Buffer controlled_buffer_7
  or or_9 (goal2, res, comparator_6_eq);
  or or_10 (or_10_out, and_7_out, and_8_out);
  D_Flip_Flop d_ff_3 (.clk(_4clk), .D(_8clk), .Q(d_ff_3_q));  // open: Qn, preset, en, reset
  not not_7 (_8clk, d_ff_3_q);
  assign controlled_buffer_8_out = and_10_out ? adder_5_out : 5'bz;  // Controlled_Buffer controlled_buffer_8
  Adder #(.width(5)) adder_5 (.a(y), .b(multiplexer_9_out), .out(adder_5_out));  // open: cin, cout
  and and_10 (and_10_out, state, ~res);  // AND_Gate
  assign controlled_buffer_6_out = and_9_out ? 5'b11100 : 5'bz;  // Controlled_Buffer controlled_buffer_9
  or or_11 (or_11_out, goal2, goal1, state);
  Register #(.width(1)) register_2 (.D(or_11_out), .Q(register_2_q), .clk(multiplexer_10_out));  // open: en, clr
  Multiplexer #(.enable("false")) multiplexer_10 (
    .in0(_16clk), .in1(_8clk), .out(multiplexer_10_out), .sel(double_speed));
  Register #(.width(1)) u_vy (
    .D(multiplexer_8_out), .en(pull_resistor_2_node), .Q(vy), .clk(controlled_inverter_1_out));  // open: clr
  assign controlled_inverter_1_out = not_8_out ? ~multiplexer_11_out : 1'bz;  // Controlled_Inverter controlled_inverter_1
  not not_8 (not_8_out, not_3_out);
  Multiplexer #(.enable("false")) multiplexer_11 (
    .in0(_32clk), .in1(_16clk), .out(multiplexer_11_out), .sel(double_speed));
  assign controlled_inverter_1_out = not_3_out ? clk : 1'bz;  // Controlled_Buffer controlled_buffer_10
  Register #(.width(1)) u_vx (.D(or_8_out), .en(collision), .Q(vx), .clk(multiplexer_12_out));  // open: clr
  Multiplexer #(.enable("false")) multiplexer_12 (
    .in0(_16clk), .in1(_8clk), .out(multiplexer_12_out), .sel(double_speed));
  and and_11 (cmb, state, or_10_out);
  not not_9 (_16clk, d_ff_4_q);
  D_Flip_Flop d_ff_4 (.clk(_8clk), .D(_16clk), .Q(d_ff_4_q));  // open: Qn, preset, en, reset
  Multiplexer #(.width(5), .enable("false")) multiplexer_13 (
    .in0(5'b01111), .in1(controlled_buffer_8_out), .out(multiplexer_13_out), .sel(and_10_out));
  Register #(.width(5)) u_x (
    .D(controlled_buffer_6_out), .en(register_2_q), .Q(x), .clk(multiplexer_14_out));  // open: clr
  Multiplexer #(.enable("false")) multiplexer_14 (
    .in0(_16clk), .in1(_8clk), .out(multiplexer_14_out), .sel(double_speed));
  D_Flip_Flop d_ff_5 (.clk(_16clk), .D(_32clk), .Q(d_ff_5_q));  // open: Qn, preset, en, reset
  not not_10 (_32clk, d_ff_5_q);
  Register #(.width(5)) u_y (.D(multiplexer_13_out), .Q(y), .clk(multiplexer_15_out));  // open: en, clr
  Multiplexer #(.enable("false")) multiplexer_15 (
    .in0(_32clk), .in1(_16clk), .out(multiplexer_15_out), .sel(double_speed));

  // Other names for the same wires on the sheet: db = double_speed; ns = nonstop; stop = move

  // Notes on the sheet:
  //   rstep
  //   score culc
  //   y collision
  //   bat culc
  //   settings
  //   y =1 - up
  //   y =0 - down
  //   x =1 - right
  //   x =0 - left
  //   x collision
  //   clock culc
  //   y_ball culc
  //   x_ball culc
endmodule

module lstep (
  input  clk,
  input  [1:0] dir,
  input  rs,
  output [4:0] lBat
);

  wire comparator_1_gt, not_1_out;
  wire [4:0] adder_1_out, controlled_buffer_1_out, multiplexer_1_out;

  Multiplexer #(.select(2), .width(5), .enable("false")) multiplexer_1 (
    .in0({5{1'b0}}), .in1(5'b00001), .in2({5{1'b1}}), .out(multiplexer_1_out), .sel(dir));  // open: in3
  Adder #(.width(5)) adder_1 (.a(multiplexer_1_out), .b(lBat), .out(adder_1_out));  // open: cin, cout
  // Probe on controlled_buffer_1_out
  assign controlled_buffer_1_out = not_1_out ? adder_1_out : 5'bz;  // Controlled_Buffer controlled_buffer_1
  not not_1 (not_1_out, rs);
  assign controlled_buffer_1_out = rs ? 5'b01110 : 5'bz;  // Controlled_Buffer controlled_buffer_2
  Comparator #(.width(5), .mode("unsigned")) comparator_1 (
    .a(5'b11110), .b(controlled_buffer_1_out), .gt(comparator_1_gt));  // open: eq, lt
  // Probe on lBat
  Register #(.width(5)) register_1 (
    .D(controlled_buffer_1_out), .en(comparator_1_gt), .Q(lBat), .clk(clk));  // open: clr
endmodule

module rstep (
  input  [6:0] keyb,
  input  clk,
  input  rs,
  output [4:0] rBat,
  output [1:0] dir
);

  wire comparator_3_gt, not_1_out;
  wire [4:0] adder_1_out, controlled_buffer_1_out, multiplexer_1_out;

  Comparator #(.width(7)) comparator_1 (.a(keyb), .b(7'b0111000), .eq(dir[0]));  // open: gt, lt
  Comparator #(.width(7)) comparator_2 (.a(keyb), .b(7'b0110010), .eq(dir[1]));  // open: gt, lt
  Multiplexer #(.select(2), .width(5), .enable("false")) multiplexer_1 (
    .in0({5{1'b0}}), .in1(5'b00001), .in2({5{1'b1}}), .out(multiplexer_1_out), .sel(dir));  // open: in3
  // Probe on controlled_buffer_1_out
  Adder #(.width(5)) adder_1 (.a(multiplexer_1_out), .b(rBat), .out(adder_1_out));  // open: cin, cout
  assign controlled_buffer_1_out = not_1_out ? adder_1_out : 5'bz;  // Controlled_Buffer controlled_buffer_1
  not not_1 (not_1_out, rs);
  Comparator #(.width(5), .mode("unsigned")) comparator_3 (
    .a(5'b11110), .b(controlled_buffer_1_out), .gt(comparator_3_gt));  // open: eq, lt
  assign controlled_buffer_1_out = rs ? 5'b01110 : 5'bz;  // Controlled_Buffer controlled_buffer_2
  // Probe on rBat
  Register #(.width(5)) register_1 (
    .D(controlled_buffer_1_out), .en(comparator_3_gt), .Q(rBat), .clk(clk));  // open: clr

  // Notes on the sheet:
  //   ascii 8
  //   ascii 2
  //   UP
  //   DOWN
endmodule

module collision (
  input  [4:0] bat,
  input  [4:0] yball,
  input  [4:0] in,
  input  [4:0] xball,
  output collision
);

  wire comparator_1_eq, comparator_2_eq, comparator_3_eq, comparator_4_eq, or_1_out;
  wire [4:0] adder_1_out, adder_2_out;

  Adder #(.width(5)) adder_1 (.a(5'b00001), .b(bat), .out(adder_1_out));  // open: cin, cout
  Adder #(.width(5)) adder_2 (.a(bat), .b(5'b00010), .out(adder_2_out));  // open: cin, cout
  Comparator #(.width(5)) comparator_1 (.a(adder_1_out), .b(yball), .eq(comparator_1_eq));  // open: gt, lt
  Comparator #(.width(5)) comparator_2 (.a(bat), .b(yball), .eq(comparator_2_eq));  // open: gt, lt
  Comparator #(.width(5)) comparator_3 (.a(adder_2_out), .b(yball), .eq(comparator_3_eq));  // open: gt, lt
  Comparator #(.width(5)) comparator_4 (.a(in), .b(xball), .eq(comparator_4_eq));  // open: gt, lt
  or or_1 (or_1_out, comparator_1_eq, comparator_2_eq, comparator_3_eq);
  and and_1 (collision, or_1_out, comparator_4_eq);
endmodule

module color (
  input  [4:0] yball,
  input  [2:0] mode,
  input  clk,
  output [31:0] out_4
);

  wire _32clk, _64clk, and_1_out, and_2_out, and_3_out, and_4_out, comparator_1_eq, d_ff_1_q, d_ff_2_q,
       d_ff_3_q, d_ff_4_q, d_ff_5_q, d_ff_6_q, not_1_out, not_2_out, not_3_out, not_4_out, undriven;
  wire [1:0] adder_1_out, register_1_q;
  wire [2:0] adder_2_out, register_2_q;
  wire [3:0] decoder_2_out3;
  wire [4:0] decoder_3_out0, or_1_out;
  wire [31:0] decoder_1_out0;

  Decoder #(.select(5)) decoder_1 (
    .out0(decoder_1_out0[0]), .out1(decoder_1_out0[1]), .out2(decoder_1_out0[2]), .out3(decoder_1_out0[3]),
    .out4(decoder_1_out0[4]), .out5(decoder_1_out0[5]), .out6(decoder_1_out0[6]), .out7(decoder_1_out0[7]),
    .out8(decoder_1_out0[8]), .out9(decoder_1_out0[9]), .out10(decoder_1_out0[10]),
    .out11(decoder_1_out0[11]), .out12(decoder_1_out0[12]), .out13(decoder_1_out0[13]),
    .out14(decoder_1_out0[14]), .out15(decoder_1_out0[15]), .out16(decoder_1_out0[16]),
    .out17(decoder_1_out0[17]), .out18(decoder_1_out0[18]), .out19(decoder_1_out0[19]),
    .out20(decoder_1_out0[20]), .out21(decoder_1_out0[21]), .out22(decoder_1_out0[22]),
    .out23(decoder_1_out0[23]), .out24(decoder_1_out0[24]), .out25(decoder_1_out0[25]),
    .out26(decoder_1_out0[26]), .out27(decoder_1_out0[27]), .out28(decoder_1_out0[28]),
    .out29(decoder_1_out0[29]), .out30(decoder_1_out0[30]), .out31(decoder_1_out0[31]), .sel(yball),
    .en(and_1_out));
  and and_1 (and_1_out, ~mode[2], ~mode[1], ~mode[0]);  // AND_Gate
  assign out_4 = and_1_out ? decoder_1_out0 : 32'bz;  // Controlled_Buffer controlled_buffer_1
  not not_1 (not_1_out, d_ff_1_q);
  D_Flip_Flop d_ff_1 (.clk(clk), .D(not_1_out), .Q(d_ff_1_q));  // open: Qn, preset, en, reset
  and and_2 (and_2_out, mode[0], ~mode[1], ~mode[2]);  // AND_Gate
  Adder #(.width(2)) adder_1 (.a(register_1_q), .b(2'b01), .out(adder_1_out));  // open: cin, cout
  not not_2 (not_2_out, d_ff_2_q);
  D_Flip_Flop d_ff_2 (.clk(not_1_out), .D(not_2_out), .Q(d_ff_2_q));  // open: Qn, preset, en, reset
  and and_3 (and_3_out, ~mode[0], mode[1], ~mode[2]);  // AND_Gate
  Register #(.width(2)) register_1 (.D(adder_1_out), .Q(register_1_q), .clk(_32clk), .clr(undriven));  // open: en
  D_Flip_Flop d_ff_3 (.clk(not_2_out), .D(not_3_out), .Q(d_ff_3_q));  // open: Qn, preset, en, reset
  Decoder #(.select(2), .enable("false")) decoder_2 (
    .out0(decoder_2_out3[0]), .out1(decoder_2_out3[1]), .out2(decoder_2_out3[2]), .out3(decoder_2_out3[3]),
    .sel(register_1_q));
  D_Flip_Flop d_ff_4 (.clk(not_3_out), .D(not_4_out), .Q(d_ff_4_q));  // open: Qn, preset, en, reset
  not not_3 (not_3_out, d_ff_3_q);
  D_Flip_Flop d_ff_5 (.clk(not_4_out), .D(_32clk), .Q(d_ff_5_q));  // open: Qn, preset, en, reset
  not not_4 (not_4_out, d_ff_4_q);
  assign out_4 = and_2_out ? {decoder_2_out3, decoder_2_out3, decoder_2_out3, decoder_2_out3, decoder_2_out3[0], decoder_2_out3[1], decoder_2_out3[2], decoder_2_out3[3], decoder_2_out3[0], decoder_2_out3[1], decoder_2_out3[2], decoder_2_out3[3], decoder_2_out3[0], decoder_2_out3[1], decoder_2_out3[2], decoder_2_out3[3], decoder_2_out3[0], decoder_2_out3[1], decoder_2_out3[2], decoder_2_out3[3]} : 32'bz;  // Controlled_Buffer controlled_buffer_2
  not not_5 (_32clk, d_ff_5_q);
  assign out_4 = and_3_out ? {decoder_2_out3[0], decoder_2_out3[1], decoder_2_out3[2], decoder_2_out3[3], decoder_2_out3[0], decoder_2_out3[1], decoder_2_out3[2], decoder_2_out3[3], decoder_2_out3[0], decoder_2_out3[1], decoder_2_out3[2], decoder_2_out3[3], decoder_2_out3[0], decoder_2_out3[1], decoder_2_out3[2], {2{decoder_2_out3[3]}}, decoder_2_out3[2:0], decoder_2_out3, decoder_2_out3, decoder_2_out3} : 32'bz;  // Controlled_Buffer controlled_buffer_3
  not not_6 (_64clk, d_ff_6_q);
  D_Flip_Flop d_ff_6 (.clk(_32clk), .D(_64clk), .Q(d_ff_6_q));  // open: Qn, preset, en, reset
  and and_4 (and_4_out, mode[0], mode[1], ~mode[2]);  // AND_Gate
  assign out_4 = and_4_out ? {decoder_3_out0[1:0], or_1_out, or_1_out, or_1_out, or_1_out, or_1_out, or_1_out} : 32'bz;  // Controlled_Buffer controlled_buffer_4
  Adder #(.width(3)) adder_2 (.a(register_2_q), .b(3'b001), .out(adder_2_out));  // open: cin, cout
  Comparator #(.width(3)) comparator_1 (.a(3'b101), .b(register_2_q), .eq(comparator_1_eq));  // open: gt, lt
  Register #(.width(3)) register_2 (
    .D(adder_2_out), .Q(register_2_q), .clk(_32clk), .clr(comparator_1_eq));  // open: en
  Decoder #(.select(3), .enable("false")) decoder_3 (
    .out0(decoder_3_out0[0]), .out1(decoder_3_out0[1]), .out2(decoder_3_out0[2]), .out3(decoder_3_out0[3]),
    .out4(decoder_3_out0[4]), .sel(register_2_q));  // open: out5, out6, out7
  assign or_1_out = decoder_3_out0 | {decoder_3_out0[0], decoder_3_out0[4:1]};  // OR_Gate or_1, 5 bits wide
endmodule

module screen (
  input  res,
  input  combo,
  input  [4:0] ballx,
  input  [4:0] bally,
  input  [4:0] left_bat,
  input  [4:0] right_bat,
  input  [7:0] lscore,
  input  [7:0] rscore,
  output [31:0] out_9,
  output [31:0] out_10,
  output [31:0] out_11,
  output [31:0] out_12,
  output [31:0] out_13,
  output [31:0] out_14,
  output [31:0] out_15,
  output [31:0] out_16,
  output [31:0] out_17,
  output [31:0] out_18,
  output [31:0] out_19,
  output [31:0] out_20,
  output [31:0] out_21,
  output [31:0] out_22,
  output [31:0] out_23,
  output [31:0] out_24,
  output [31:0] out_25,
  output [31:0] out_26,
  output [31:0] out_27,
  output [31:0] out_28,
  output [31:0] out_29,
  output [31:0] out_30,
  output [31:0] out_31,
  output [31:0] out_32,
  output [31:0] out_33,
  output [31:0] out_34,
  output [31:0] out_35,
  output [31:0] out_36,
  output [31:0] out_37,
  output [31:0] out_38,
  output [31:0] out_39,
  output move,
  output [31:0] out_41,
  output [31:0] color
);

  wire and_1_out, and_3_out, and_4_out, and_5_out, and_6_out, clock_1_out, clock_2_out, clock_3_out,
       comparator_1_lt, or_1_out;
  wire [2:0] multiplexer_1_out, multiplexer_2_out, state_q;
  wire [2:1] comparator_2_lt;
  wire [4:0] n8rows_1_out_14, n8rows_1_out_15, n8rows_1_out_16, n8rows_1_out_17, n8rows_1_out_18,
       n8rows_2_out_14, n8rows_2_out_15, n8rows_2_out_16, n8rows_2_out_17, n8rows_2_out_18, n8rows_3_out_14,
       n8rows_3_out_15, n8rows_3_out_16, n8rows_3_out_17, n8rows_3_out_18;
  wire [7:0] counter_1_q;
  wire [31:0] n8rows_1_out_6, n8rows_1_out_7, n8rows_1_out_8, n8rows_1_out_9, n8rows_1_out_10,
       n8rows_1_out_11, n8rows_1_out_12, n8rows_1_out_13, n8rows_2_out_6, n8rows_2_out_7, n8rows_2_out_8,
       n8rows_2_out_9, n8rows_2_out_10, n8rows_2_out_11, n8rows_2_out_12, n8rows_2_out_13, n8rows_3_out_6,
       n8rows_3_out_7, n8rows_3_out_8, n8rows_3_out_9, n8rows_3_out_10, n8rows_3_out_11, n8rows_3_out_12,
       n8rows_3_out_13, n8rows_4_out_6, n8rows_4_out_7, n8rows_4_out_8, n8rows_4_out_9, n8rows_4_out_10,
       n8rows_4_out_11, n8rows_4_out_12, n8rows_4_out_13;

  and and_1 (and_1_out, ~comparator_1_lt, clock_1_out);  // AND_Gate
  Clock clock_1 (.out(clock_1_out));
  Counter counter_1 (.count(and_1_out), .Q(counter_1_q), .clk(and_1_out), .clr(res));  // open: load, D, carry
  Comparator #(.mode("unsigned")) comparator_1 (.a(8'hfe), .b(counter_1_q), .lt(comparator_1_lt));  // open: gt, eq
  or or_1 (or_1_out, comparator_2_lt[1], comparator_2_lt[2]);
  and and_2 (move, ~or_1_out, comparator_1_lt);  // AND_Gate
  Clock clock_2 (.out(clock_2_out));
  Multiplexer #(.select(3), .width(3), .enable("false")) multiplexer_1 (
    .in0(3'b010), .in1(3'b000), .in2(3'b001), .in3(3'b001), .in4(3'b001), .in5(3'b001), .in6(3'b001),
    .in7(3'b001), .out(multiplexer_1_out), .sel(state_q));
  Multiplexer #(.width(3), .enable("false")) multiplexer_2 (
    .in0(multiplexer_1_out), .in1(3'b011), .out(multiplexer_2_out), .sel(combo));
  Comparator #(.mode("unsigned")) comparator_2 (.a(8'h10), .b(lscore), .lt(comparator_2_lt[1]));  // open: gt, eq
  Comparator #(.mode("unsigned")) comparator_3 (.a(rscore), .b(8'h10), .gt(comparator_2_lt[2]));  // open: eq, lt
  Register #(.width(3)) state (.D({comparator_2_lt, move}), .Q(state_q), .clk(clock_2_out), .clr(res));  // open: en
  color color_1 (.yball(bally), .mode(multiplexer_2_out), .clk(clock_3_out), .out_4(color));
  Clock clock_3 (.out(clock_3_out));
  and and_3 (and_3_out, state_q[0], ~state_q[1], ~state_q[2]);  // AND_Gate
  assign out_38 = and_3_out ? n8rows_1_out_6 : 32'bz;  // Controlled_Buffer controlled_buffer_1
  assign out_26 = and_3_out ? n8rows_1_out_12 : 32'bz;  // Controlled_Buffer controlled_buffer_2
  assign out_32 = and_3_out ? n8rows_1_out_9 : 32'bz;  // Controlled_Buffer controlled_buffer_3
  assign out_11 = and_3_out ? n8rows_2_out_7 : 32'bz;  // Controlled_Buffer controlled_buffer_4
  assign out_14 = and_3_out ? n8rows_2_out_10 : 32'bz;  // Controlled_Buffer controlled_buffer_5
  assign out_23 = and_3_out ? n8rows_3_out_11 : 32'bz;  // Controlled_Buffer controlled_buffer_6
  assign out_20 = and_3_out ? n8rows_3_out_8 : 32'bz;  // Controlled_Buffer controlled_buffer_7
  assign out_17 = and_3_out ? n8rows_2_out_13 : 32'bz;  // Controlled_Buffer controlled_buffer_8
  assign out_27 = and_3_out ? n8rows_4_out_6 : 32'bz;  // Controlled_Buffer controlled_buffer_9
  assign out_39 = and_3_out ? n8rows_4_out_12 : 32'bz;  // Controlled_Buffer controlled_buffer_10
  assign out_33 = and_3_out ? n8rows_4_out_9 : 32'bz;  // Controlled_Buffer controlled_buffer_11
  assign out_28 = and_3_out ? n8rows_1_out_11 : 32'bz;  // Controlled_Buffer controlled_buffer_12
  assign out_34 = and_3_out ? n8rows_1_out_8 : 32'bz;  // Controlled_Buffer controlled_buffer_13
  _8rows u_8rows_1 (
    .in_1({5{1'b0}}), .in_2(ballx), .in_3(bally), .in_4(left_bat), .in_5(right_bat), .out_6(n8rows_1_out_6),
    .out_7(n8rows_1_out_7), .out_8(n8rows_1_out_8), .out_9(n8rows_1_out_9), .out_10(n8rows_1_out_10),
    .out_11(n8rows_1_out_11), .out_12(n8rows_1_out_12), .out_13(n8rows_1_out_13), .out_14(n8rows_1_out_14),
    .out_15(n8rows_1_out_15), .out_16(n8rows_1_out_16), .out_17(n8rows_1_out_17), .out_18(n8rows_1_out_18));
  assign out_16 = and_3_out ? n8rows_2_out_12 : 32'bz;  // Controlled_Buffer controlled_buffer_14
  assign out_13 = and_3_out ? n8rows_2_out_9 : 32'bz;  // Controlled_Buffer controlled_buffer_15
  assign out_10 = and_3_out ? n8rows_2_out_6 : 32'bz;  // Controlled_Buffer controlled_buffer_16
  _8rows u_8rows_2 (
    .in_1(n8rows_1_out_14), .in_2(n8rows_1_out_15), .in_3(n8rows_1_out_16), .in_4(n8rows_1_out_17),
    .in_5(n8rows_1_out_18), .out_6(n8rows_2_out_6), .out_7(n8rows_2_out_7), .out_8(n8rows_2_out_8),
    .out_9(n8rows_2_out_9), .out_10(n8rows_2_out_10), .out_11(n8rows_2_out_11), .out_12(n8rows_2_out_12),
    .out_13(n8rows_2_out_13), .out_14(n8rows_2_out_14), .out_15(n8rows_2_out_15), .out_16(n8rows_2_out_16),
    .out_17(n8rows_2_out_17), .out_18(n8rows_2_out_18));
  assign out_19 = and_3_out ? n8rows_3_out_7 : 32'bz;  // Controlled_Buffer controlled_buffer_17
  assign out_25 = and_3_out ? n8rows_3_out_13 : 32'bz;  // Controlled_Buffer controlled_buffer_18
  assign out_22 = and_3_out ? n8rows_3_out_10 : 32'bz;  // Controlled_Buffer controlled_buffer_19
  _8rows u_8rows_3 (
    .in_1(n8rows_2_out_14), .in_2(n8rows_2_out_15), .in_3(n8rows_2_out_16), .in_4(n8rows_2_out_17),
    .in_5(n8rows_2_out_18), .out_6(n8rows_3_out_6), .out_7(n8rows_3_out_7), .out_8(n8rows_3_out_8),
    .out_9(n8rows_3_out_9), .out_10(n8rows_3_out_10), .out_11(n8rows_3_out_11), .out_12(n8rows_3_out_12),
    .out_13(n8rows_3_out_13), .out_14(n8rows_3_out_14), .out_15(n8rows_3_out_15), .out_16(n8rows_3_out_16),
    .out_17(n8rows_3_out_17), .out_18(n8rows_3_out_18));
  assign out_37 = and_3_out ? n8rows_4_out_11 : 32'bz;  // Controlled_Buffer controlled_buffer_20
  assign out_31 = and_3_out ? n8rows_4_out_8 : 32'bz;  // Controlled_Buffer controlled_buffer_21
  _8rows u_8rows_4 (
    .in_1(n8rows_3_out_14), .in_2(n8rows_3_out_15), .in_3(n8rows_3_out_16), .in_4(n8rows_3_out_17),
    .in_5(n8rows_3_out_18), .out_6(n8rows_4_out_6), .out_7(n8rows_4_out_7), .out_8(n8rows_4_out_8),
    .out_9(n8rows_4_out_9), .out_10(n8rows_4_out_10), .out_11(n8rows_4_out_11), .out_12(n8rows_4_out_12),
    .out_13(n8rows_4_out_13));  // open: out_14, out_15, out_16, out_17, out_18
  assign out_9 = and_3_out ? n8rows_1_out_13 : 32'bz;  // Controlled_Buffer controlled_buffer_22
  assign out_30 = and_3_out ? n8rows_1_out_10 : 32'bz;  // Controlled_Buffer controlled_buffer_23
  assign out_36 = and_3_out ? n8rows_1_out_7 : 32'bz;  // Controlled_Buffer controlled_buffer_24
  assign out_12 = and_3_out ? n8rows_2_out_8 : 32'bz;  // Controlled_Buffer controlled_buffer_25
  assign out_18 = and_3_out ? n8rows_3_out_6 : 32'bz;  // Controlled_Buffer controlled_buffer_26
  assign out_15 = and_3_out ? n8rows_2_out_11 : 32'bz;  // Controlled_Buffer controlled_buffer_27
  assign out_21 = and_3_out ? n8rows_3_out_9 : 32'bz;  // Controlled_Buffer controlled_buffer_28
  assign out_24 = and_3_out ? n8rows_3_out_12 : 32'bz;  // Controlled_Buffer controlled_buffer_29
  assign out_41 = and_3_out ? n8rows_4_out_13 : 32'bz;  // Controlled_Buffer controlled_buffer_30
  assign out_29 = and_3_out ? n8rows_4_out_7 : 32'bz;  // Controlled_Buffer controlled_buffer_31
  assign out_35 = and_3_out ? n8rows_4_out_10 : 32'bz;  // Controlled_Buffer controlled_buffer_32
  and and_4 (and_4_out, ~state_q[0], ~state_q[1], ~state_q[2]);  // AND_Gate
  assign out_38 = and_4_out ? {32{1'b0}} : 32'bz;  // Controlled_Buffer controlled_buffer_33
  assign out_36 = and_4_out ? 32'h40000000 : 32'bz;  // Controlled_Buffer controlled_buffer_34
  assign out_34 = and_4_out ? 32'h40e00004 : 32'bz;  // Controlled_Buffer controlled_buffer_35
  assign out_32 = and_4_out ? 32'h7ca0000a : 32'bz;  // Controlled_Buffer controlled_buffer_36
  assign out_30 = and_4_out ? 32'h40e00011 : 32'bz;  // Controlled_Buffer controlled_buffer_37
  assign out_28 = and_4_out ? 32'h40000021 : 32'bz;  // Controlled_Buffer controlled_buffer_38
  assign out_26 = and_4_out ? 32'h42 : 32'bz;  // Controlled_Buffer controlled_buffer_39
  assign out_9 = and_4_out ? 32'h7c000084 : 32'bz;  // Controlled_Buffer controlled_buffer_40
  assign out_10 = and_4_out ? 32'h5403f108 : 32'bz;  // Controlled_Buffer controlled_buffer_41
  assign out_11 = and_4_out ? 32'h540c0f10 : 32'bz;  // Controlled_Buffer controlled_buffer_42
  assign out_12 = and_4_out ? 32'h441001a0 : 32'bz;  // Controlled_Buffer controlled_buffer_43
  assign out_13 = and_4_out ? 32'h2000c0 : 32'bz;  // Controlled_Buffer controlled_buffer_44
  assign out_14 = and_4_out ? 32'h7c400080 : 32'bz;  // Controlled_Buffer controlled_buffer_45
  assign out_15 = and_4_out ? 32'h20800080 : 32'bz;  // Controlled_Buffer controlled_buffer_46
  assign out_16 = and_4_out ? 32'h11000080 : 32'bz;  // Controlled_Buffer controlled_buffer_47
  assign out_17 = and_4_out ? 32'h7d000040 : 32'bz;  // Controlled_Buffer controlled_buffer_48
  assign out_18 = and_4_out ? 32'h1000040 : 32'bz;  // Controlled_Buffer controlled_buffer_49
  assign out_19 = and_4_out ? 32'h7d000040 : 32'bz;  // Controlled_Buffer controlled_buffer_50
  assign out_20 = and_4_out ? 32'h21000040 : 32'bz;  // Controlled_Buffer controlled_buffer_51
  assign out_21 = and_4_out ? 32'h11000040 : 32'bz;  // Controlled_Buffer controlled_buffer_52
  assign out_22 = and_4_out ? 32'h7d000040 : 32'bz;  // Controlled_Buffer controlled_buffer_53
  assign out_23 = and_4_out ? 32'h1000080 : 32'bz;  // Controlled_Buffer controlled_buffer_54
  assign out_24 = and_4_out ? 32'h44800100 : 32'bz;  // Controlled_Buffer controlled_buffer_55
  assign out_25 = and_4_out ? 32'h7c800200 : 32'bz;  // Controlled_Buffer controlled_buffer_56
  assign out_27 = and_4_out ? 32'h44400400 : 32'bz;  // Controlled_Buffer controlled_buffer_57
  assign out_29 = and_4_out ? 32'h301800 : 32'bz;  // Controlled_Buffer controlled_buffer_58
  assign out_31 = and_4_out ? 32'h340fe000 : 32'bz;  // Controlled_Buffer controlled_buffer_59
  assign out_33 = and_4_out ? 32'h54000000 : 32'bz;  // Controlled_Buffer controlled_buffer_60
  assign out_35 = and_4_out ? 32'h54000000 : 32'bz;  // Controlled_Buffer controlled_buffer_61
  assign out_37 = and_4_out ? 32'h54000000 : 32'bz;  // Controlled_Buffer controlled_buffer_62
  assign out_39 = and_4_out ? 32'h58000000 : 32'bz;  // Controlled_Buffer controlled_buffer_63
  assign out_41 = and_4_out ? {32{1'b0}} : 32'bz;  // Controlled_Buffer controlled_buffer_64
  and and_5 (and_5_out, ~state_q[0], state_q[1], ~state_q[2]);  // AND_Gate
  assign out_38 = and_5_out ? {32{1'b0}} : 32'bz;  // Controlled_Buffer controlled_buffer_65
  assign out_36 = and_5_out ? 32'h7f000000 : 32'bz;  // Controlled_Buffer controlled_buffer_66
  assign out_34 = and_5_out ? 32'h48000000 : 32'bz;  // Controlled_Buffer controlled_buffer_67
  assign out_32 = and_5_out ? 32'h48000000 : 32'bz;  // Controlled_Buffer controlled_buffer_68
  assign out_30 = and_5_out ? 32'h78000000 : 32'bz;  // Controlled_Buffer controlled_buffer_69
  assign out_28 = and_5_out ? 32'h1c000 : 32'bz;  // Controlled_Buffer controlled_buffer_70
  assign out_26 = and_5_out ? 32'h11012000 : 32'bz;  // Controlled_Buffer controlled_buffer_71
  assign out_9 = and_5_out ? 32'h21011000 : 32'bz;  // Controlled_Buffer controlled_buffer_72
  assign out_10 = and_5_out ? 32'h7f030800 : 32'bz;  // Controlled_Buffer controlled_buffer_73
  assign out_11 = and_5_out ? 32'h103fc00 : 32'bz;  // Controlled_Buffer controlled_buffer_74
  assign out_12 = and_5_out ? 32'h1040200 : 32'bz;  // Controlled_Buffer controlled_buffer_75
  assign out_13 = and_5_out ? 32'h82104 : 32'bz;  // Controlled_Buffer controlled_buffer_76
  assign out_14 = and_5_out ? 32'h70181087 : 32'bz;  // Controlled_Buffer controlled_buffer_77
  assign out_15 = and_5_out ? 32'he28887c : 32'bz;  // Controlled_Buffer controlled_buffer_78
  assign out_16 = and_5_out ? 32'h1680804 : 32'bz;  // Controlled_Buffer controlled_buffer_79
  assign out_17 = and_5_out ? 32'h7e680804 : 32'bz;  // Controlled_Buffer controlled_buffer_80
  assign out_18 = and_5_out ? 32'h128887c : 32'bz;  // Controlled_Buffer controlled_buffer_81
  assign out_19 = and_5_out ? 32'he181087 : 32'bz;  // Controlled_Buffer controlled_buffer_82
  assign out_20 = and_5_out ? 32'h70082104 : 32'bz;  // Controlled_Buffer controlled_buffer_83
  assign out_21 = and_5_out ? 32'h40200 : 32'bz;  // Controlled_Buffer controlled_buffer_84
  assign out_22 = and_5_out ? 32'h4103fc00 : 32'bz;  // Controlled_Buffer controlled_buffer_85
  assign out_23 = and_5_out ? 32'h41030800 : 32'bz;  // Controlled_Buffer controlled_buffer_86
  assign out_24 = and_5_out ? 32'h7f011000 : 32'bz;  // Controlled_Buffer controlled_buffer_87
  assign out_25 = and_5_out ? 32'h41012000 : 32'bz;  // Controlled_Buffer controlled_buffer_88
  assign out_27 = and_5_out ? 32'h4101c000 : 32'bz;  // Controlled_Buffer controlled_buffer_89
  assign out_29 = and_5_out ? {32{1'b0}} : 32'bz;  // Controlled_Buffer controlled_buffer_90
  assign out_31 = and_5_out ? 32'h7f000000 : 32'bz;  // Controlled_Buffer controlled_buffer_91
  assign out_33 = and_5_out ? 32'h20000000 : 32'bz;  // Controlled_Buffer controlled_buffer_92
  assign out_35 = and_5_out ? 32'h10000000 : 32'bz;  // Controlled_Buffer controlled_buffer_93
  assign out_37 = and_5_out ? 32'h8000000 : 32'bz;  // Controlled_Buffer controlled_buffer_94
  assign out_39 = and_5_out ? 32'h7f000000 : 32'bz;  // Controlled_Buffer controlled_buffer_95
  assign out_41 = and_5_out ? {32{1'b0}} : 32'bz;  // Controlled_Buffer controlled_buffer_96
  and and_6 (and_6_out, ~state_q[0], ~state_q[1], state_q[2]);  // AND_Gate
  assign out_38 = and_6_out ? {32{1'b0}} : 32'bz;  // Controlled_Buffer controlled_buffer_97
  assign out_36 = and_6_out ? 32'h7f000000 : 32'bz;  // Controlled_Buffer controlled_buffer_98
  assign out_34 = and_6_out ? 32'h48000000 : 32'bz;  // Controlled_Buffer controlled_buffer_99
  assign out_32 = and_6_out ? 32'h48000000 : 32'bz;  // Controlled_Buffer controlled_buffer_100
  assign out_30 = and_6_out ? 32'h78000000 : 32'bz;  // Controlled_Buffer controlled_buffer_101
  assign out_28 = and_6_out ? 32'h1c000 : 32'bz;  // Controlled_Buffer controlled_buffer_102
  assign out_26 = and_6_out ? 32'h21012000 : 32'bz;  // Controlled_Buffer controlled_buffer_103
  assign out_9 = and_6_out ? 32'h43011000 : 32'bz;  // Controlled_Buffer controlled_buffer_104
  assign out_10 = and_6_out ? 32'h45030800 : 32'bz;  // Controlled_Buffer controlled_buffer_105
  assign out_11 = and_6_out ? 32'h4903fc00 : 32'bz;  // Controlled_Buffer controlled_buffer_106
  assign out_12 = and_6_out ? 32'h31040200 : 32'bz;  // Controlled_Buffer controlled_buffer_107
  assign out_13 = and_6_out ? 32'h82104 : 32'bz;  // Controlled_Buffer controlled_buffer_108
  assign out_14 = and_6_out ? 32'h70181087 : 32'bz;  // Controlled_Buffer controlled_buffer_109
  assign out_15 = and_6_out ? 32'he28887c : 32'bz;  // Controlled_Buffer controlled_buffer_110
  assign out_16 = and_6_out ? 32'h1680804 : 32'bz;  // Controlled_Buffer controlled_buffer_111
  assign out_17 = and_6_out ? 32'h7e680804 : 32'bz;  // Controlled_Buffer controlled_buffer_112
  assign out_18 = and_6_out ? 32'h128887c : 32'bz;  // Controlled_Buffer controlled_buffer_113
  assign out_19 = and_6_out ? 32'he181087 : 32'bz;  // Controlled_Buffer controlled_buffer_114
  assign out_20 = and_6_out ? 32'h70082104 : 32'bz;  // Controlled_Buffer controlled_buffer_115
  assign out_21 = and_6_out ? 32'h40200 : 32'bz;  // Controlled_Buffer controlled_buffer_116
  assign out_22 = and_6_out ? 32'h4103fc00 : 32'bz;  // Controlled_Buffer controlled_buffer_117
  assign out_23 = and_6_out ? 32'h41030800 : 32'bz;  // Controlled_Buffer controlled_buffer_118
  assign out_24 = and_6_out ? 32'h7f011000 : 32'bz;  // Controlled_Buffer controlled_buffer_119
  assign out_25 = and_6_out ? 32'h41012000 : 32'bz;  // Controlled_Buffer controlled_buffer_120
  assign out_27 = and_6_out ? 32'h4101c000 : 32'bz;  // Controlled_Buffer controlled_buffer_121
  assign out_29 = and_6_out ? {32{1'b0}} : 32'bz;  // Controlled_Buffer controlled_buffer_122
  assign out_31 = and_6_out ? 32'h7f000000 : 32'bz;  // Controlled_Buffer controlled_buffer_123
  assign out_33 = and_6_out ? 32'h20000000 : 32'bz;  // Controlled_Buffer controlled_buffer_124
  assign out_35 = and_6_out ? 32'h10000000 : 32'bz;  // Controlled_Buffer controlled_buffer_125
  assign out_37 = and_6_out ? 32'h8000000 : 32'bz;  // Controlled_Buffer controlled_buffer_126
  assign out_39 = and_6_out ? 32'h7f000000 : 32'bz;  // Controlled_Buffer controlled_buffer_127
  assign out_41 = and_6_out ? {32{1'b0}} : 32'bz;  // Controlled_Buffer controlled_buffer_128

  // Other names for the same wires on the sheet: port1[31:0] = out_38; port2[31:0] = out_36; port3[31:0] = out_34;
  //   port4[31:0] = out_32; port5[31:0] = out_30; port6[31:0] = out_28; port7[31:0] = out_26; port8[31:0] = out_9;
  //   port9[31:0] = out_10; port10[31:0] = out_11; port11[31:0] = out_12; port12[31:0] = out_13;
  //   port13[31:0] = out_14; port14[31:0] = out_15; port15[31:0] = out_16; port16[31:0] = out_17;
  //   port17[31:0] = out_18; port18[31:0] = out_19; port19[31:0] = out_20; port20[31:0] = out_21;
  //   port21[31:0] = out_22; port22[31:0] = out_23; port23[31:0] = out_24; port24[31:0] = out_25;
  //   port25[31:0] = out_27; port26[31:0] = out_29; port27[31:0] = out_31; port28[31:0] = out_33;
  //   port29[31:0] = out_35; port30[31:0] = out_37; port31[31:0] = out_39; port32[31:0] = out_41; y[4:0] = bally

  // Notes on the sheet:
  //   000 - y ball
  //   001 - gravity
  //   010 reverse grav
  //   011 - fire
  //   start
  //   p1 win
  //   p2 win
endmodule
